// Logisim project regfile.circ as structural Verilog: 1 circuit, main circuit regfile
module regfile (
  input  [4:0] ReadIndex1,
  input  [4:0] ReadIndex2,
  input  [4:0] WriteIndex,
  input  [31:0] WriteData,
  input  RegWEn,
  input  clk,
  output [31:0] ra,
  output [31:0] sp,
  output [31:0] t0,
  output [31:0] t1,
  output [31:0] t2,
  output [31:0] s0,
  output [31:0] s1,
  output [31:0] a0,
  output [31:0] ReadData1,
  output [31:0] ReadData2
);

  wire x1w, x2w, x3w, x4w, x5w, x6w, x7w, x8w, x9w, x10w, x11w, x12w, x13w, x14w, x15w, x16w, x17w, x18w,
       x19w, x20w, x21w, x22w, x23w, x24w, x25w, x26w, x27w, x28w, x29w, x30w, x31w;
  wire [31:0] x3out, x4out, x11out, x12out, x13out, x14out, x15out, x16out, x17out, x18out, x19out, x20out,
       x21out, x22out, x23out, x24out, x25out, x26out, x27out, x28out, x29out, x30out, x31out;

  Decoder #(.select(5)) decoder_1 (
    .out1(x1w), .out2(x2w), .out3(x3w), .out4(x4w), .out5(x5w), .out6(x6w), .out7(x7w), .out8(x8w),
    .out9(x9w), .out10(x10w), .out11(x11w), .out12(x12w), .out13(x13w), .out14(x14w), .out15(x15w),
    .out16(x16w), .out17(x17w), .out18(x18w), .out19(x19w), .out20(x20w), .out21(x21w), .out22(x22w),
    .out23(x23w), .out24(x24w), .out25(x25w), .out26(x26w), .out27(x27w), .out28(x28w), .out29(x29w),
    .out30(x30w), .out31(x31w), .sel(WriteIndex), .en(RegWEn));  // open: out0
  Multiplexer #(.select(5), .width(32)) multiplexer_1 (
    .in0({32{1'b0}}), .in1(ra), .in2(sp), .in3(x3out), .in4(x4out), .in5(t0), .in6(t1), .in7(t2), .in8(s0),
    .in9(s1), .in10(a0), .in11(x11out), .in12(x12out), .in13(x13out), .in14(x14out), .in15(x15out),
    .in16(x16out), .in17(x17out), .in18(x18out), .in19(x19out), .in20(x20out), .in21(x21out), .in22(x22out),
    .in23(x23out), .in24(x24out), .in25(x25out), .in26(x26out), .in27(x27out), .in28(x28out), .in29(x29out),
    .in30(x30out), .in31(x31out), .out(ReadData1), .sel(ReadIndex1));
  Multiplexer #(.select(5), .width(32)) multiplexer_2 (
    .in0({32{1'b0}}), .in1(ra), .in2(sp), .in3(x3out), .in4(x4out), .in5(t0), .in6(t1), .in7(t2), .in8(s0),
    .in9(s1), .in10(a0), .in11(x11out), .in12(x12out), .in13(x13out), .in14(x14out), .in15(x15out),
    .in16(x16out), .in17(x17out), .in18(x18out), .in19(x19out), .in20(x20out), .in21(x21out), .in22(x22out),
    .in23(x23out), .in24(x24out), .in25(x25out), .in26(x26out), .in27(x27out), .in28(x28out), .in29(x29out),
    .in30(x30out), .in31(x31out), .out(ReadData2), .sel(ReadIndex2));
  Register #(.width(32)) register_1 (.D(WriteData), .en(x9w), .clk(clk), .Q(s1));  // open: clr
  Register #(.width(32)) register_2 (.D(WriteData), .en(x17w), .clk(clk), .Q(x17out));  // open: clr
  Register #(.width(32)) register_3 (.D(WriteData), .en(x25w), .clk(clk), .Q(x25out));  // open: clr
  Register #(.width(32)) register_4 (.D(WriteData), .en(x1w), .clk(clk), .Q(ra));  // open: clr
  Register #(.width(32)) register_5 (.D(WriteData), .en(x2w), .clk(clk), .Q(sp));  // open: clr
  Register #(.width(32)) register_6 (.D(WriteData), .en(x10w), .clk(clk), .Q(a0));  // open: clr
  Register #(.width(32)) register_7 (.D(WriteData), .en(x18w), .clk(clk), .Q(x18out));  // open: clr
  Register #(.width(32)) register_8 (.D(WriteData), .en(x26w), .clk(clk), .Q(x26out));  // open: clr
  Register #(.width(32)) register_9 (.D(WriteData), .en(x3w), .clk(clk), .Q(x3out));  // open: clr
  Register #(.width(32)) register_10 (.D(WriteData), .en(x11w), .clk(clk), .Q(x11out));  // open: clr
  Register #(.width(32)) register_11 (.D(WriteData), .en(x19w), .clk(clk), .Q(x19out));  // open: clr
  Register #(.width(32)) register_12 (.D(WriteData), .en(x27w), .clk(clk), .Q(x27out));  // open: clr
  Register #(.width(32)) register_13 (.D(WriteData), .en(x4w), .clk(clk), .Q(x4out));  // open: clr
  Register #(.width(32)) register_14 (.D(WriteData), .en(x12w), .clk(clk), .Q(x12out));  // open: clr
  Register #(.width(32)) register_15 (.D(WriteData), .en(x20w), .clk(clk), .Q(x20out));  // open: clr
  Register #(.width(32)) register_16 (.D(WriteData), .en(x28w), .clk(clk), .Q(x28out));  // open: clr
  Register #(.width(32)) register_17 (.D(WriteData), .en(x5w), .clk(clk), .Q(t0));  // open: clr
  Register #(.width(32)) register_18 (.D(WriteData), .en(x13w), .clk(clk), .Q(x13out));  // open: clr
  Register #(.width(32)) register_19 (.D(WriteData), .en(x21w), .clk(clk), .Q(x21out));  // open: clr
  Register #(.width(32)) register_20 (.D(WriteData), .en(x29w), .clk(clk), .Q(x29out));  // open: clr
  Register #(.width(32)) register_21 (.D(WriteData), .en(x6w), .clk(clk), .Q(t1));  // open: clr
  Register #(.width(32)) register_22 (.D(WriteData), .en(x14w), .clk(clk), .Q(x14out));  // open: clr
  Register #(.width(32)) register_23 (.D(WriteData), .en(x22w), .clk(clk), .Q(x22out));  // open: clr
  Register #(.width(32)) register_24 (.D(WriteData), .en(x30w), .clk(clk), .Q(x30out));  // open: clr
  Register #(.width(32)) register_25 (.D(WriteData), .en(x7w), .clk(clk), .Q(t2));  // open: clr
  Register #(.width(32)) register_26 (.D(WriteData), .en(x15w), .clk(clk), .Q(x15out));  // open: clr
  Register #(.width(32)) register_27 (.D(WriteData), .en(x23w), .clk(clk), .Q(x23out));  // open: clr
  Register #(.width(32)) register_28 (.D(WriteData), .en(x31w), .clk(clk), .Q(x31out));  // open: clr
  Register #(.width(32)) register_29 (.D(WriteData), .en(x8w), .clk(clk), .Q(s0));  // open: clr
  Register #(.width(32)) register_30 (.D(WriteData), .en(x16w), .clk(clk), .Q(x16out));  // open: clr
  Register #(.width(32)) register_31 (.D(WriteData), .en(x24w), .clk(clk), .Q(x24out));  // open: clr

  // Other names for the same wires on the sheet: x1out[31:0] = ra; x2out[31:0] = sp; x5out[31:0] = t0;
  //   x6out[31:0] = t1; x7out[31:0] = t2; x8out[31:0] = s0; x9out[31:0] = s1; x10out[31:0] = a0

  // Notes on the sheet:
  //   INPUTS to your circuit
  //   DON'T CHANGE THE LOCATIONS OF THE INPUTS AND OUTPUTS!
  //   These are DEBUG/TEST outputs from your circuit.
  //   OUTPUTS from your circuit
endmodule
